// Logisim project Guia_1100.circ as structural Verilog: 1 circuit, main circuit main
module main (
  input  pulso,
  input  CLR,
  output Mealy,
  output Moore
);

  wire CLK_out, d_ff_1_q, d_ff_2_q, d_ff_3_q, d_ff_3_qn, d_ff_4_q, d_ff_5_q, d_ff_6_q, d_ff_6_qn, d_ff_7_q,
       d_ff_8_q, d_ff_9_q;

  Clock CLK (.out(CLK_out));
  D_Flip_Flop d_ff_1 (.clk(CLK_out), .D(pulso), .Q(d_ff_1_q), .reset(CLR));  // open: Qn, preset
  D_Flip_Flop d_ff_2 (.clk(CLK_out), .D(pulso), .Q(d_ff_2_q), .reset(CLR));  // open: Qn, preset
  and and_1 (Mealy, d_ff_7_q, d_ff_5_q, d_ff_3_qn, d_ff_1_q);
  and and_2 (Moore, d_ff_9_q, d_ff_8_q, d_ff_6_qn, d_ff_4_q);
  D_Flip_Flop d_ff_3 (.clk(CLK_out), .D(d_ff_1_q), .Q(d_ff_3_q), .Qn(d_ff_3_qn), .reset(CLR));  // open: preset
  D_Flip_Flop d_ff_4 (.clk(CLK_out), .D(d_ff_2_q), .Q(d_ff_4_q), .reset(CLR));  // open: Qn, preset
  D_Flip_Flop d_ff_5 (.clk(CLK_out), .D(d_ff_3_q), .Q(d_ff_5_q), .reset(CLR));  // open: Qn, preset
  D_Flip_Flop d_ff_6 (.clk(CLK_out), .D(d_ff_4_q), .Q(d_ff_6_q), .Qn(d_ff_6_qn), .reset(CLR));  // open: preset
  D_Flip_Flop d_ff_7 (.clk(CLK_out), .D(d_ff_5_q), .Q(d_ff_7_q), .reset(CLR));  // open: Qn, preset
  D_Flip_Flop d_ff_8 (.clk(CLK_out), .D(d_ff_6_q), .Q(d_ff_8_q), .reset(CLR));  // open: Qn, preset
  D_Flip_Flop d_ff_9 (.clk(CLK_out), .D(d_ff_8_q), .Q(d_ff_9_q), .reset(CLR));  // open: Qn, preset
endmodule
