// Logisim project Guia_1105.circ as structural Verilog: 1 circuit, main circuit main
module main (
  input  RESET,
  input  x,
  input  CLK,
  input  z
);

  // D_Flip_Flop #(.enable("true")) d_ff_1: pin names not known; wires that end beside it: RESET
  // AND_Gate and_1 is placed but not wired

  assign x = CLK;
  assign z = CLK;
endmodule
