// Logisim project Guia_1304.circ as structural Verilog: 1 circuit, main circuit main
module main (
  input  _1,
  input  Clear
);

  wire and_1_out, and_2_out, j_k_ff_1_q, j_k_ff_1_qn, j_k_ff_2_q, j_k_ff_2_qn, j_k_ff_3_q, j_k_ff_3_qn,
       j_k_ff_4_q, not_1_out, not_2_out, Pulse_out;

  Button Pulse (.out(Pulse_out));
  and and_1 (and_1_out, Clear, and_2_out);
  and and_2 (and_2_out, j_k_ff_1_q, not_1_out, j_k_ff_3_q, not_2_out);
  // Probe on j_k_ff_4_q
  J_K_Flip_Flop j_k_ff_1 (
    .J(_1), .clk(Pulse_out), .K(_1), .Q(j_k_ff_1_q), .Qn(j_k_ff_1_qn), .reset(and_1_out));  // open: preset
  not not_1 (not_1_out, j_k_ff_2_q);
  not not_2 (not_2_out, j_k_ff_4_q);
  // Probe on j_k_ff_3_q
  J_K_Flip_Flop j_k_ff_2 (
    .J(_1), .clk(j_k_ff_1_qn), .K(_1), .Q(j_k_ff_2_q), .Qn(j_k_ff_2_qn), .reset(and_1_out));  // open: preset
  // Probe on j_k_ff_2_q
  J_K_Flip_Flop j_k_ff_3 (
    .J(_1), .clk(j_k_ff_2_qn), .K(_1), .Q(j_k_ff_3_q), .Qn(j_k_ff_3_qn), .reset(and_1_out));  // open: preset
  // Probe on j_k_ff_1_q
  J_K_Flip_Flop j_k_ff_4 (.J(_1), .clk(j_k_ff_3_qn), .K(_1), .Q(j_k_ff_4_q), .reset(and_1_out));  // open: Qn, preset

  // Notes on the sheet:
  //   Contador Assíncrono Decádico Crescente de 4 bits
endmodule
