// Logisim project Guia_1305.circ as structural Verilog: 1 circuit, main circuit main
module main (
  input  Clear
);

  wire and_1_out, Clock_out, or_1_out, t_ff_1_q, t_ff_2_q, t_ff_2_qn, t_ff_3_q, t_ff_3_qn;

  Clock Clock (.out(Clock_out));
  or or_1 (or_1_out, Clear, and_1_out);
  // Probe on t_ff_1_q
  T_Flip_Flop t_ff_1 (.clk(t_ff_2_qn), .T(t_ff_2_qn), .Q(t_ff_1_q), .reset(or_1_out));  // open: Qn, preset
  and and_1 (and_1_out, t_ff_1_q, t_ff_2_q, t_ff_3_q);
  // Probe on t_ff_2_q
  T_Flip_Flop t_ff_2 (.clk(t_ff_3_qn), .T(t_ff_3_qn), .Q(t_ff_2_q), .Qn(t_ff_2_qn), .reset(or_1_out));  // open: preset
  T_Flip_Flop t_ff_3 (.clk(Clock_out), .T(Clock_out), .Q(t_ff_3_q), .Qn(t_ff_3_qn), .reset(or_1_out));  // open: preset
  // Probe on t_ff_3_q

  // Notes on the sheet:
  //   Contador Síncrono Módulo 7
endmodule
