// Logisim project Guia_1307.circ as structural Verilog: 1 circuit, main circuit main
module main (
  input  Input,
  input  Clear
);

  wire Clock_out, j_k_ff_1_q, j_k_ff_1_qn, j_k_ff_2_q, j_k_ff_2_qn, j_k_ff_3_q, j_k_ff_3_qn, j_k_ff_4_q,
       j_k_ff_4_qn, j_k_ff_5_q, j_k_ff_5_qn, not_1_out, or_1_out;

  Clock Clock (.out(Clock_out));
  or or_1 (or_1_out, Input, j_k_ff_5_qn);
  not not_1 (not_1_out, or_1_out);
  J_K_Flip_Flop j_k_ff_1 (
    .J(or_1_out), .clk(Clock_out), .K(not_1_out), .Q(j_k_ff_1_q), .Qn(j_k_ff_1_qn), .reset(Clear));  // open: preset
  J_K_Flip_Flop j_k_ff_2 (
    .J(j_k_ff_1_q), .clk(Clock_out), .K(j_k_ff_1_qn), .Q(j_k_ff_2_q), .Qn(j_k_ff_2_qn), .reset(Clear));  // open: preset
  J_K_Flip_Flop j_k_ff_3 (
    .J(j_k_ff_2_q), .clk(Clock_out), .K(j_k_ff_2_qn), .Q(j_k_ff_3_q), .Qn(j_k_ff_3_qn), .reset(Clear));  // open: preset
  J_K_Flip_Flop j_k_ff_4 (
    .J(j_k_ff_3_q), .clk(Clock_out), .K(j_k_ff_3_qn), .Q(j_k_ff_4_q), .Qn(j_k_ff_4_qn), .reset(Clear));  // open: preset
  // Probe on j_k_ff_1_q
  // Probe on j_k_ff_4_q
  // Probe on j_k_ff_2_q
  // Probe on j_k_ff_3_q
  J_K_Flip_Flop j_k_ff_5 (
    .J(j_k_ff_4_q), .clk(Clock_out), .K(j_k_ff_4_qn), .Q(j_k_ff_5_q), .Qn(j_k_ff_5_qn), .reset(Clear));  // open: preset
  // Probe on j_k_ff_5_q

  // Notes on the sheet:
  //   Contador em Anel Torcido de 5 bits
endmodule
