// Logisim project P02_04d.circ as structural Verilog: 1 circuit, main circuit main
module main (
  input  A,
  input  B,
  input  C,
  output OUT
);

  wire and_1_out, and_2_out, not_1_out, not_2_out;

  not not_1 (not_1_out, A);
  and and_1 (and_1_out, not_1_out, not_2_out, C);
  not not_2 (not_2_out, B);
  and and_2 (and_2_out, A, B, C);
  or or_1 (OUT, and_1_out, and_2_out);
endmodule
