// Logisim project Rec-0101e.circ as structural Verilog: 1 circuit, main circuit main
module main (
  input  x,
  input  y,
  input  w,
  input  z,
  output s
);

  wire nand_1_out, nand_2_out, nand_3_out, nand_4_out, nand_5_out, nand_6_out, nw_out, nz_out;

  nand nw (nw_out, w, w);
  nand nz (nz_out, z, z);
  nand nand_1 (nand_1_out, x, nw_out);
  nand nand_2 (nand_2_out, y, nw_out);
  nand nand_3 (nand_3_out, x, y);
  nand nand_4 (nand_4_out, nand_2_out, z);
  nand nand_5 (nand_5_out, nand_3_out, nz_out);
  nand nand_6 (nand_6_out, nand_1_out, nand_4_out);
  nand nand_7 (s, nand_6_out, nand_5_out);

  // Notes on the sheet:
  //   Term1
  //   Term4
  //   Term2
  //   Term3
  //   Term5
endmodule
