// Logisim project Rec-0103b.circ as structural Verilog: 1 circuit, main circuit main
module main (
  input  x,
  input  y,
  output s
);

  wire and_1_out, and_3_out, not_1_out, not_2_out, not_3_out, not_4_out, not_5_out;

  not not_1 (not_1_out, x);
  not not_2 (not_2_out, x);
  not not_3 (not_3_out, y);
  and and_1 (and_1_out, not_1_out, y);
  not not_4 (not_4_out, and_1_out);
  and and_2 (s, not_4_out, not_5_out);
  not not_5 (not_5_out, and_3_out);
  and and_3 (and_3_out, not_2_out, not_3_out);
endmodule
