// Logisim project Guia_1102.circ as structural Verilog: 1 circuit, main circuit main
module main (
  input  pulso,
  input  CLR,
  output out_3
);

  wire and_1_out, CLK_out, d_ff_1_q, d_ff_1_qn, d_ff_2_q, d_ff_3_q, d_ff_3_qn, d_ff_4_q, d_ff_5_qn;

  Clock CLK (.out(CLK_out));
  D_Flip_Flop d_ff_1 (.clk(CLK_out), .D(pulso), .Q(d_ff_1_q), .Qn(d_ff_1_qn), .reset(CLR));  // open: preset
  D_Flip_Flop d_ff_2 (.clk(CLK_out), .D(d_ff_1_q), .Q(d_ff_2_q), .reset(CLR));  // open: Qn, preset
  D_Flip_Flop d_ff_3 (.clk(CLK_out), .D(d_ff_2_q), .Q(d_ff_3_q), .Qn(d_ff_3_qn), .reset(CLR));  // open: preset
  D_Flip_Flop d_ff_4 (.clk(CLK_out), .D(d_ff_3_q), .Q(d_ff_4_q), .reset(CLR));  // open: Qn, preset
  and and_1 (and_1_out, d_ff_4_q, d_ff_3_qn, d_ff_2_q, d_ff_1_qn);
  D_Flip_Flop #(.trigger("falling"), .enable("true")) d_ff_5 (
    .clk(CLK_out), .D(and_1_out), .Qn(d_ff_5_qn), .en(d_ff_5_qn), .reset(CLR));  // open: Q, preset
  and and_2 (out_3, d_ff_5_qn, and_1_out);

  // Notes on the sheet:
  //   Found
endmodule
