// Logisim project Guia_1301.circ as structural Verilog: 1 circuit, main circuit main
module main (
  input  _1,
  input  Clear
);

  wire j_k_ff_1_qn, j_k_ff_2_qn, j_k_ff_3_qn, j_k_ff_4_qn, j_k_ff_5_qn, Pulse_out;

  Button Pulse (.out(Pulse_out));
  // Probe on j_k_ff_1_qn
  J_K_Flip_Flop j_k_ff_1 (.J(_1), .clk(j_k_ff_2_qn), .K(_1), .Qn(j_k_ff_1_qn), .reset(Clear));  // open: Q, preset
  J_K_Flip_Flop j_k_ff_2 (.J(_1), .clk(j_k_ff_3_qn), .K(_1), .Qn(j_k_ff_2_qn), .reset(Clear));  // open: Q, preset
  // Probe on j_k_ff_2_qn
  // Probe on j_k_ff_3_qn
  J_K_Flip_Flop j_k_ff_3 (.J(_1), .clk(j_k_ff_4_qn), .K(_1), .Qn(j_k_ff_3_qn), .reset(Clear));  // open: Q, preset
  // Probe on j_k_ff_4_qn
  J_K_Flip_Flop j_k_ff_4 (.J(_1), .clk(j_k_ff_5_qn), .K(_1), .Qn(j_k_ff_4_qn), .reset(Clear));  // open: Q, preset
  // Probe on j_k_ff_5_qn
  J_K_Flip_Flop j_k_ff_5 (.J(_1), .clk(Pulse_out), .K(_1), .Qn(j_k_ff_5_qn), .reset(Clear));  // open: Q, preset

  // Notes on the sheet:
  //   Contador Assíncrono Decrescente de 5 bits
endmodule
