// Logisim project Guia-0801.circ as structural Verilog: 2 circuits, main circuit main
module main (
  input  A,
  input  B,
  input  CarryIn,
  output Soma,
  output CarryOut
);

  wire H1_s0, H1_s1, half_adder_1_s1;

  Half_adder H1 (.A(A), .B(B), .s0(H1_s0), .s1(H1_s1));
  Half_adder half_adder_1 (.A(H1_s0), .B(CarryIn), .s0(Soma), .s1(half_adder_1_s1));
  or or_1 (CarryOut, H1_s1, half_adder_1_s1);
endmodule

module Half_adder (
  input  A,
  input  B,
  output s0,
  output s1
);

  and and_1 (s0, A, B);
  xor xor_1 (s1, A, B);
endmodule
