// Logisim project Guia-0802.circ as structural Verilog: 1 circuit, main circuit main
module main (
  input  A,
  input  B,
  input  CarryIn,
  output Diff,
  output BorrowOut
);

  wire and_1_out, not_1_out;

  and and_1 (and_1_out, A, not_1_out);
  not not_1 (not_1_out, B);
  xor xor_1 (Diff, A, B);
  or or_1 (BorrowOut, and_1_out, and_1_out);
endmodule
