// Logisim project Guia-0803.circ as structural Verilog
module comparador (
  input  X0,
  input  X1,
  input  X2,
  input  X3,
  input  X4,
  input  Y0,
  input  Y1,
  input  Y2,
  input  Y3,
  input  Y4,
  output equal
);

  // XNOR_Gate xnor_1 is placed but not wired
  // XNOR_Gate xnor_2 is placed but not wired
  // XNOR_Gate xnor_3 is placed but not wired
  // XNOR_Gate xnor_4 is placed but not wired
  // XNOR_Gate xnor_5 is placed but not wired
  // AND_Gate and_1 has open pins: out=equal
endmodule
