// Logisim project Rec-0101c.circ as structural Verilog: 1 circuit, main circuit main
module main (
  input  x,
  input  y,
  input  w,
  input  z,
  output S
);

  wire and_1_out, and_2_out, and_3_out, not_1_out, not_2_out, not_3_out, not_4_out;

  not not_1 (not_1_out, w);
  not not_2 (not_2_out, w);
  not not_3 (not_3_out, z);
  not not_4 (not_4_out, z);
  and and_1 (and_1_out, x, not_1_out);
  and and_2 (and_2_out, y, not_2_out, not_3_out);
  and and_3 (and_3_out, x, y, not_4_out);
  or or_1 (S, and_1_out, and_2_out, and_3_out);
endmodule
