// Logisim project Rec-0101d.circ as structural Verilog: 1 circuit, main circuit main
module main (
  input  X,
  input  Y,
  input  W,
  input  Z,
  output S
);

  wire not_1_out, not_2_out, not_3_out, not_4_out, not_5_out, or_1_out, or_2_out, or_3_out, or_4_out,
       or_5_out;

  or or_1 (or_1_out, X, Y);
  or or_2 (or_2_out, X, not_1_out);
  not not_1 (not_1_out, Z);
  or or_3 (or_3_out, X, not_2_out);
  not not_2 (not_2_out, W);
  not not_3 (not_3_out, W);
  or or_4 (or_4_out, not_3_out, not_4_out);
  not not_4 (not_4_out, Z);
  or or_5 (or_5_out, Y, not_5_out);
  not not_5 (not_5_out, W);
  and and_1 (S, or_1_out, or_2_out, or_3_out, or_4_out, or_5_out);
endmodule
