// Logisim project Rec-0101f.circ as structural Verilog: 1 circuit, main circuit main
module main (
  input  X,
  input  Y,
  input  W,
  input  Z,
  output S
);

  wire nor_1_out, nor_2_out, nor_3_out, nor_4_out, nor_5_out, nor_6_out, nor_7_out, nor_8_out, nW_out, nZ_out;

  nor nW (nW_out, W, W);
  nor nZ (nZ_out, Z, Z);
  nor nor_1 (nor_1_out, X, Y);
  nor nor_2 (nor_2_out, nor_1_out, nor_3_out);
  nor nor_3 (nor_3_out, X, nZ_out);
  nor nor_4 (nor_4_out, X, nW_out);
  nor nor_5 (nor_5_out, nor_4_out, nor_6_out);
  nor nor_6 (nor_6_out, nW_out, nZ_out);
  nor nor_7 (nor_7_out, Y, nW_out);
  nor nor_8 (nor_8_out, nor_2_out, nor_5_out);
  nor nor_9 (S, nor_8_out, nor_7_out);

  // Notes on the sheet:
  //   Term1
  //   Term2
  //   Term3
  //   Term4
  //   Term5
endmodule
