// Logisim project Rec-0102a.circ as structural Verilog: 1 circuit, main circuit main
module main (
  input  a,
  input  c,
  output out_3
);

  wire not_1_out;

  not not_1 (not_1_out, a);
  Multiplexer #(.enable("false")) multiplexer_1 (.in0(a), .in1(not_1_out), .out(out_3), .sel(c));
endmodule
