// Logisim project Rec-0102b.circ as structural Verilog: 1 circuit, main circuit main
module main (
  input  a,
  input  b,
  input  c,
  output s
);

  wire multiplexer_1_out, not_1_out, not_2_out;

  Multiplexer #(.enable("false")) multiplexer_1 (.in0(a), .in1(not_1_out), .out(multiplexer_1_out), .sel(b));
  not not_1 (not_1_out, a);
  Multiplexer #(.enable("false")) multiplexer_2 (.in0(c), .in1(not_2_out), .out(s), .sel(multiplexer_1_out));
  not not_2 (not_2_out, c);
endmodule
