// Logisim project receba.circ as structural Verilog: 8 circuits, main circuit main
module main (
  input  A0,
  input  A1,
  input  CI,
  input  A2,
  input  A3,
  input  B0,
  input  B1,
  input  B2,
  input  B3,
  output S0,
  output S1,
  output S2,
  output S3,
  output Carry_Out,
  output Overflow
);

  wire decodificador_1_a_2, decodificador_1_b_2, decodificador_1_c_2, decodificador_1_d_2, decodificador_1_e,
       decodificador_1_f, decodificador_1_g, decodificador_2_a_2, decodificador_2_b_2, decodificador_2_c_2,
       decodificador_2_d_2, decodificador_2_e, decodificador_2_f, decodificador_2_g, decodificador_3_a_2,
       decodificador_3_b_2, decodificador_3_c_2, decodificador_3_d_2, decodificador_3_e, decodificador_3_f,
       decodificador_3_g;

  decodificador decodificador_1 (
    .A(A3), .B(A2), .C(A1), .a_2(decodificador_1_a_2), .D(A0), .b_2(decodificador_1_b_2),
    .c_2(decodificador_1_c_2), .d_2(decodificador_1_d_2), .e(decodificador_1_e), .f(decodificador_1_f),
    .g(decodificador_1_g));
  somador_4_bits somador_4_bits_1 (
    .B3(B3), .A3(A3), .B2(B2), .A2(A2), .B1(B1), .A1(A1), .B0(B0), .A0(A0), .Carry_Out(Carry_Out), .S3(S3),
    .S2(S2), .S1(S1), .S0(S0), .Carry_In(CI), .Overflow(Overflow));
  decodificador decodificador_2 (
    .A(B3), .B(B2), .C(B1), .a_2(decodificador_2_a_2), .D(B0), .b_2(decodificador_2_b_2),
    .c_2(decodificador_2_c_2), .d_2(decodificador_2_d_2), .e(decodificador_2_e), .f(decodificador_2_f),
    .g(decodificador_2_g));
  _7_Segment_Display u_7_segment_display_1 (
    .g(decodificador_1_g), .f(decodificador_1_f), .a(decodificador_1_a_2), .b(decodificador_1_b_2),
    .e(decodificador_1_e), .d(decodificador_1_d_2), .c(decodificador_1_c_2));  // open: dp
  _7_Segment_Display u_7_segment_display_2 (
    .g(decodificador_2_g), .f(decodificador_2_f), .a(decodificador_2_a_2), .b(decodificador_2_b_2),
    .e(decodificador_2_e), .d(decodificador_2_d_2), .c(decodificador_2_c_2));  // open: dp
  decodificador decodificador_3 (
    .A(S3), .B(S2), .C(S1), .a_2(decodificador_3_a_2), .D(S0), .b_2(decodificador_3_b_2),
    .c_2(decodificador_3_c_2), .d_2(decodificador_3_d_2), .e(decodificador_3_e), .f(decodificador_3_f),
    .g(decodificador_3_g));
  _7_Segment_Display u_7_segment_display_3 (
    .g(decodificador_3_g), .f(decodificador_3_f), .a(decodificador_3_a_2), .b(decodificador_3_b_2),
    .e(decodificador_3_e), .d(decodificador_3_d_2), .c(decodificador_3_c_2));  // open: dp
endmodule

// HA
module meia_soma (
  input  A0,
  input  B0,
  output Sum,
  output Carry_Out
);

  xor \xor  (Sum, A0, B0);
  and \and  (Carry_Out, A0, B0);

  // Notes on the sheet:
  //   Circuito de Meia Soma - Half Adder
endmodule

// FA
module soma_completa (
  input  Carry_In,
  input  A0,
  input  B0,
  output Sum,
  output Carry_Out
);

  wire meia_soma_1_carry_out, meia_soma_1_sum, meia_soma_2_carry_out;

  meia_soma meia_soma_1 (.A0(A0), .B0(B0), .Sum(meia_soma_1_sum), .Carry_Out(meia_soma_1_carry_out));
  meia_soma meia_soma_2 (.A0(Carry_In), .B0(meia_soma_1_sum), .Sum(Sum), .Carry_Out(meia_soma_2_carry_out));
  or \or  (Carry_Out, meia_soma_2_carry_out, meia_soma_1_carry_out);

  // Notes on the sheet:
  //   Circuito de Soma Completa - Full Adder
endmodule

// somador 4 bits
module somador_4_bits (
  input  A3,
  input  A2,
  input  A1,
  input  A0,
  input  B3,
  input  B2,
  input  B1,
  input  B0,
  input  Carry_In,
  output Carry_Out,
  output S3,
  output S2,
  output S1,
  output S0,
  output Overflow
);

  wire soma_completa_2_carry_out, soma_completa_3_carry_out, soma_completa_4_carry_out;

  soma_completa soma_completa_1 (
    .Carry_In(soma_completa_2_carry_out), .A0(A3), .B0(B3), .Sum(S3), .Carry_Out(Carry_Out));
  xor \xor  (Overflow, Carry_Out, soma_completa_2_carry_out);
  soma_completa soma_completa_2 (
    .Carry_In(soma_completa_3_carry_out), .A0(A2), .B0(B2), .Sum(S2), .Carry_Out(soma_completa_2_carry_out));
  soma_completa soma_completa_3 (
    .Carry_In(soma_completa_4_carry_out), .A0(A1), .B0(B1), .Sum(S1), .Carry_Out(soma_completa_3_carry_out));
  soma_completa soma_completa_4 (
    .Carry_In(Carry_In), .A0(A0), .B0(B0), .Sum(S0), .Carry_Out(soma_completa_4_carry_out));

  // Notes on the sheet:
  //   Circuito do Somador de 4 bits
endmodule

module decodificador (
  input  A,
  input  B,
  input  C,
  input  D,
  output a_2,
  output b_2,
  output c_2,
  output d_2,
  output e,
  output f,
  output g
);

  wire and_1_out, and_2_out, and_3_out, and_4_out, and_5_out, and_6_out, and_7_out, and_8_out, and_9_out,
       and_10_out, and_11_out, and_12_out, and_13_out, and_14_out, and_15_out, and_16_out, and_17_out,
       and_18_out, and_19_out, and_20_out, and_21_out, and_22_out, and_23_out, and_24_out, and_25_out,
       and_26_out, and_27_out, and_28_out, and_29_out, and_30_out, and_31_out, and_32_out, and_33_out,
       and_34_out, and_35_out, not_1_out, not_2_out, not_3_out, not_4_out, not_5_out, not_6_out, not_7_out,
       not_8_out, not_9_out, not_10_out, not_11_out, not_12_out, not_13_out, not_14_out, not_15_out,
       not_16_out, not_17_out, not_18_out, not_19_out, not_20_out, not_21_out, not_22_out, not_23_out,
       not_24_out, not_25_out, not_26_out, not_27_out, not_28_out, not_29_out, not_30_out, not_31_out,
       not_32_out, not_33_out, not_34_out, not_35_out, not_36_out, not_37_out, not_38_out, not_39_out,
       not_40_out, not_41_out, not_42_out, not_43_out, not_44_out;

  not not_1 (not_1_out, B);
  and and_1 (and_1_out, not_1_out, not_2_out);
  not not_2 (not_2_out, D);
  not not_3 (not_3_out, A);
  and and_2 (and_2_out, not_3_out, C);
  not not_4 (not_4_out, A);
  and and_3 (and_3_out, not_4_out, B, D);
  and and_4 (and_4_out, B, C);
  not not_5 (not_5_out, B);
  and and_5 (and_5_out, A, not_5_out, not_6_out);
  not not_6 (not_6_out, C);
  and and_6 (and_6_out, A, not_7_out);
  not not_7 (not_7_out, D);
  not not_8 (not_8_out, A);
  and and_7 (and_7_out, not_8_out, not_9_out);
  not not_9 (not_9_out, B);
  not not_10 (not_10_out, A);
  and and_8 (and_8_out, not_10_out, not_11_out, not_12_out);
  not not_11 (not_11_out, C);
  not not_12 (not_12_out, D);
  not not_13 (not_13_out, B);
  and and_9 (and_9_out, not_13_out, not_14_out);
  not not_14 (not_14_out, D);
  not not_15 (not_15_out, A);
  and and_10 (and_10_out, not_15_out, C, D);
  and and_11 (and_11_out, A, not_16_out, D);
  not not_16 (not_16_out, C);
  not not_17 (not_17_out, A);
  and and_12 (and_12_out, not_17_out, not_18_out);
  not not_18 (not_18_out, C);
  not not_19 (not_19_out, A);
  and and_13 (and_13_out, not_19_out, D);
  not not_20 (not_20_out, C);
  and and_14 (and_14_out, not_20_out, D);
  not not_21 (not_21_out, A);
  and and_15 (and_15_out, not_21_out, B);
  and and_16 (and_16_out, A, not_22_out);
  not not_22 (not_22_out, B);
  not not_23 (not_23_out, A);
  and and_17 (and_17_out, not_23_out, not_24_out, not_25_out);
  not not_24 (not_24_out, B);
  not not_25 (not_25_out, D);
  not not_26 (not_26_out, B);
  and and_18 (and_18_out, not_26_out, C, D);
  and and_19 (and_19_out, B, not_27_out, D);
  not not_27 (not_27_out, C);
  and and_20 (and_20_out, B, C, not_28_out);
  not not_28 (not_28_out, D);
  not not_29 (not_29_out, C);
  and and_21 (and_21_out, A, not_29_out, not_30_out);
  not not_30 (not_30_out, D);
  not not_31 (not_31_out, B);
  and and_22 (and_22_out, not_31_out, not_32_out);
  not not_32 (not_32_out, D);
  and and_23 (and_23_out, C, not_33_out);
  not not_33 (not_33_out, D);
  and and_24 (and_24_out, A, C);
  and and_25 (and_25_out, A, B);
  not not_34 (not_34_out, C);
  and and_26 (and_26_out, not_34_out, not_35_out);
  not not_35 (not_35_out, D);
  not not_36 (not_36_out, A);
  and and_27 (and_27_out, not_36_out, B, not_37_out);
  not not_37 (not_37_out, C);
  and and_28 (and_28_out, B, not_38_out);
  not not_38 (not_38_out, D);
  and and_29 (and_29_out, A, not_39_out);
  not not_39 (not_39_out, B);
  and and_30 (and_30_out, A, C);
  not not_40 (not_40_out, B);
  and and_31 (and_31_out, not_40_out, C);
  and and_32 (and_32_out, C, not_41_out);
  not not_41 (not_41_out, D);
  not not_42 (not_42_out, A);
  and and_33 (and_33_out, not_42_out, B, not_43_out);
  not not_43 (not_43_out, C);
  and and_34 (and_34_out, A, not_44_out);
  not not_44 (not_44_out, B);
  and and_35 (and_35_out, A, D);
  or or_1 (b_2, and_7_out, and_8_out, and_9_out, and_10_out, and_11_out);
  or or_2 (c_2, and_12_out, and_13_out, and_14_out, and_15_out, and_16_out);
  or or_3 (d_2, and_17_out, and_18_out, and_19_out, and_20_out, and_21_out);
  or or_4 (e, and_22_out, and_23_out, and_24_out, and_25_out);
  or or_5 (f, and_26_out, and_27_out, and_28_out, and_29_out, and_30_out);
  or or_6 (g, and_31_out, and_32_out, and_33_out, and_34_out, and_35_out);
  or or_7 (a_2, and_1_out, and_2_out, and_3_out, and_4_out, and_5_out, and_6_out);
endmodule

module atv_aula (
  input  [3:0] OP,
  input  [3:0] A,
  input  [3:0] B,
  output [3:0] S,
  output out_5,
  output out_6
);

  wire [3:0] adder_1_out, adder_2_out, and_1_out, and_2_out, and_3_out, nand_1_out, nor_1_out, not_1_out,
       not_2_out, not_3_out, not_4_out, not_5_out, not_6_out, not_7_out, or_1_out, or_2_out, or_3_out;

  assign not_1_out = ~A;  // NOT_Gate not_1, 4 bits wide
  assign nor_1_out = ~(A | B);  // NOR_Gate nor_1, 4 bits wide
  assign not_2_out = ~A;  // NOT_Gate not_2, 4 bits wide
  Multiplexer #(.select(4), .width(4), .enable("false")) multiplexer_1 (
    .in0(not_1_out), .in1(nor_1_out), .in2(and_1_out), .in3(4'b0000), .in4(nand_1_out), .in5(not_3_out),
    .in6(adder_1_out), .in7(and_2_out), .in8(or_1_out), .in9(not_6_out), .in10(B), .in11(and_3_out),
    .in12(4'b1111), .in13(or_2_out), .in14(or_3_out), .in15(A), .out(S), .sel(OP));
  assign and_1_out = not_2_out & B;  // AND_Gate and_1, 4 bits wide
  assign nand_1_out = ~(A & B);  // NAND_Gate nand_1, 4 bits wide
  assign not_3_out = ~B;  // NOT_Gate not_3, 4 bits wide
  Adder #(.width(4)) adder_1 (.a(A), .b(B), .out(adder_1_out), .cin(1'b0), .cout(out_5));
  assign and_2_out = A & not_4_out;  // AND_Gate and_2, 4 bits wide
  assign or_1_out = not_5_out | B;  // OR_Gate or_1, 4 bits wide
  assign not_4_out = ~B;  // NOT_Gate not_4, 4 bits wide
  assign not_5_out = ~A;  // NOT_Gate not_5, 4 bits wide
  Adder #(.width(4)) adder_2 (.a(A), .b(B), .out(adder_2_out), .cin(1'b0), .cout(out_6));
  assign not_6_out = ~adder_2_out;  // NOT_Gate not_6, 4 bits wide
  assign and_3_out = A & B;  // AND_Gate and_3, 4 bits wide
  assign or_2_out = A | not_7_out;  // OR_Gate or_2, 4 bits wide
  assign or_3_out = A | B;  // OR_Gate or_3, 4 bits wide
  assign not_7_out = ~B;  // NOT_Gate not_7, 4 bits wide
endmodule

module ULA_1_bit (
  input  CarryIn,
  input  A,
  input  B,
  input  [1:0] OP_1_e_2,
  input  Binvert,
  output S,
  output CarryOut
);

  wire and_1_out, multiplexer_1_out, not_1_out, not_2_out, or_1_out, soma_completa_1_sum;

  not not_1 (not_1_out, B);
  and and_1 (and_1_out, A, multiplexer_1_out);
  or or_1 (or_1_out, A, multiplexer_1_out);
  not not_2 (not_2_out, A);
  Multiplexer #(.enable("false")) multiplexer_1 (.in0(B), .in1(not_1_out), .out(multiplexer_1_out), .sel(Binvert));
  soma_completa soma_completa_1 (
    .Carry_In(CarryIn), .A0(A), .B0(multiplexer_1_out), .Sum(soma_completa_1_sum), .Carry_Out(CarryOut));
  Multiplexer #(.select(2), .enable("false")) multiplexer_2 (
    .in0(and_1_out), .in1(or_1_out), .in2(not_2_out), .in3(soma_completa_1_sum), .out(S), .sel(OP_1_e_2));

  // Notes on the sheet:
  //   ULA Cauã
endmodule

module ULA_4_bits (
  input  CarryIn,
  input  Binvert,
  input  [1:0] OP_1_e_2,
  input  A0,
  input  B0,
  input  A1,
  input  B1,
  input  A2,
  input  B2,
  input  A3,
  input  B3,
  output S0,
  output S1,
  output S2,
  output S3,
  output CarryOut
);

  wire ula_1_bit_1_carryout, ula_1_bit_2_carryout, ula_1_bit_3_carryout;

  ULA_1_bit ula_1_bit_1 (
    .A(A0), .B(B0), .CarryIn(CarryIn), .Binvert(Binvert), .CarryOut(ula_1_bit_1_carryout), .S(S0),
    .OP_1_e_2(OP_1_e_2));
  ULA_1_bit ula_1_bit_2 (
    .A(A1), .B(B1), .CarryIn(ula_1_bit_1_carryout), .Binvert(Binvert), .CarryOut(ula_1_bit_2_carryout),
    .S(S1), .OP_1_e_2(OP_1_e_2));
  ULA_1_bit ula_1_bit_3 (
    .A(A2), .B(B2), .CarryIn(ula_1_bit_2_carryout), .Binvert(Binvert), .CarryOut(ula_1_bit_3_carryout),
    .S(S2), .OP_1_e_2(OP_1_e_2));
  ULA_1_bit ula_1_bit_4 (
    .A(A3), .B(B3), .CarryIn(ula_1_bit_3_carryout), .Binvert(Binvert), .CarryOut(CarryOut), .S(S3),
    .OP_1_e_2(OP_1_e_2));
endmodule
